# Fritzing sketch Elektronik Roboter (saved by Fritzing 0.9.3b)
breadboards: 1

parts:
  M2 = DC Motor
  IC1 = L293D [package=THT]
  hc-sr1 = hc-sr04
  Bauteil1 = Arduino Nano (Rev3.0) (ICSP)
  VCC1 = 4 x AAA Battery Mount
  M1 = DC Motor
  U1 = SWITCH-SPST-2 [package=switch-spst-vertical]

nets:
  N1: M2.pin_1, IC1.Out_4_(_Controlled_by_Enable_2_)
  N2: M2.pin_2, IC1.Out_3_(_Controlled_by_Enable_2_)
  VCC: IC1.Enable_1, IC1.Enable_2, IC1.+V, hc-sr1.VCC, Bauteil1.5V
  N3: IC1.In_1, Bauteil1.D2
  N4: IC1.Out_1_(_Controlled_by_Enable_1_), M1.pin_1
  GND: IC1.0V, hc-sr1.GND, Bauteil1.GND, VCC1.-
  N5: IC1.Out_2_(_Controlled_by_Enable_1_), M1.pin_2
  N6: IC1.In_2, Bauteil1.D3
  N7: IC1.+Vmotor, Bauteil1.VIN, U1.O
  N8: IC1.In_3, Bauteil1.D5
  N9: IC1.In_4, Bauteil1.D4
  N10: hc-sr1.Trig, Bauteil1.D8
  N11: hc-sr1.Echo, Bauteil1.D9
  N12: VCC1.+, U1.P
